// Logisim project DustcatV.circ as structural Verilog
module CPU (
);

  wire architecturalregisterfile_1_written, button_1_out, clock_1_out, reorderbuffer_1_entry_available,
       reorderbuffer_1_ready;
  wire [3:0] bit_extender_5_out, decodeissue_1_decode_dest, decodeissue_1_decode_qj, decodeissue_1_decode_qk,
       reorderbuffer_1_inst_id_out;
  wire [7:0] bit_extender_2_out, bit_extender_3_out, bit_extender_4_out, decodeissue_1_decode_op,
       reorderbuffer_1_rob_dest;
  wire [15:0] decodeissue_1_decode_const;
  wire [23:0] bit_extender_1_out;
  wire [31:0] architecturalregisterfile_1_arf_a, architecturalregisterfile_1_arf_b, bit_extender_6_out,
       instructionfetch_1_inst_out, instructionfetch_1_next_adress, reorderbuffer_1_rob_result, rom_1_data;
  wire [39:0] execute_1_cbdout1, execute_1_cdbout2, execute_1_cdbout3lsu, forwardingunit_1_cbd1,
       forwardingunit_1_cbd2;

  Button button_1 (.out(button_1_out));
  Clock clock_1 (.out(clock_1_out));
  ROM #(.addrWidth(24), .dataWidth(32)) rom_1 (.addr(bit_extender_1_out), .data(rom_1_data));
  InstructionFetch instructionfetch_1 (
    .RST(button_1_out), .CLK_IN(clock_1_out), .LOAD_NEXT(reorderbuffer_1_entry_available),
    .DATA_IN(rom_1_data), .INST_OUT(instructionfetch_1_inst_out), .NEXT_ADRESS(instructionfetch_1_next_adress));  // open: JUMP_ADRESS, LOAD_ADRESS
  Bit_Extender #(.in_width(32), .out_width(24)) bit_extender_1 (
    .in(instructionfetch_1_next_adress), .out(bit_extender_1_out));
  DecodeIssue decodeissue_1 (
    .CLK_IN(clock_1_out), .INST_IN(instructionfetch_1_inst_out), .DECODE_OP(decodeissue_1_decode_op),
    .DECODE_DEST(decodeissue_1_decode_dest), .DECODE_QJ(decodeissue_1_decode_qj),
    .DECODE_QK(decodeissue_1_decode_qk), .DECODE_CONST(decodeissue_1_decode_const));
  assign bit_extender_2_out = {{4{decodeissue_1_decode_dest[3]}}, decodeissue_1_decode_dest};  // Bit_Extender bit_extender_2
  assign bit_extender_3_out = {{4{decodeissue_1_decode_qj[3]}}, decodeissue_1_decode_qj};  // Bit_Extender bit_extender_3
  assign bit_extender_4_out = {{4{decodeissue_1_decode_qk[3]}}, decodeissue_1_decode_qk};  // Bit_Extender bit_extender_4
  Bit_Extender #(.out_width(4)) bit_extender_5 (.in(reorderbuffer_1_rob_dest), .out(bit_extender_5_out));
  assign bit_extender_6_out = {{16{decodeissue_1_decode_const[15]}}, decodeissue_1_decode_const};  // Bit_Extender bit_extender_6
  ReorderBuffer reorderbuffer_1 (
    .CLK_IN(clock_1_out), .OP_IN(decodeissue_1_decode_op), .DEST(bit_extender_2_out), .RESET(button_1_out),
    .CBD1_IN(execute_1_cbdout1), .CBD2_IN(execute_1_cdbout2), .CBD3_IN(execute_1_cdbout3lsu),
    .WRITTEN_CONFIRM(architecturalregisterfile_1_written), .ENTRY_AVAILABLE(reorderbuffer_1_entry_available),
    .READY(reorderbuffer_1_ready), .INST_ID_OUT(reorderbuffer_1_inst_id_out),
    .ROB_DEST(reorderbuffer_1_rob_dest), .ROB_RESULT(reorderbuffer_1_rob_result));
  ArchitecturalRegisterFile architecturalregisterfile_1 (
    .ARF_Data(reorderbuffer_1_rob_result), .ARF_A_Sel(decodeissue_1_decode_qj),
    .ARF_B_Sel(decodeissue_1_decode_qk), .ARF_Write_Sel(bit_extender_5_out),
    .ARF_Write(reorderbuffer_1_ready), .ARF_Clk(clock_1_out), .RESET(button_1_out),
    .ARF_A(architecturalregisterfile_1_arf_a), .ARF_B(architecturalregisterfile_1_arf_b),
    .WRITTEN(architecturalregisterfile_1_written));
  ForwardingUnit forwardingunit_1 (
    .CLK(clock_1_out), .ROB_REG(reorderbuffer_1_rob_dest), .ROB_VALUE(reorderbuffer_1_rob_result),
    .INST_DEST(decodeissue_1_decode_dest), .REGA_IN(decodeissue_1_decode_qj),
    .REGB_IN(decodeissue_1_decode_qk), .ARF_A_IN(architecturalregisterfile_1_arf_a),
    .ARF_B_IN(architecturalregisterfile_1_arf_b), .WRITE_ROB(reorderbuffer_1_ready), .RST(button_1_out),
    .CBD1IN(execute_1_cbdout1), .CBD2IN(execute_1_cdbout2), .CBD3IN(execute_1_cdbout3lsu),
    .CBD1(forwardingunit_1_cbd1), .CBD2(forwardingunit_1_cbd2));
  Execute execute_1 (
    .Ex_OPIN(decodeissue_1_decode_op), .EX_DESTIN(bit_extender_2_out), .EX_QJIN(bit_extender_3_out),
    .EX_QKIN(bit_extender_4_out), .EX_CONST_IN(bit_extender_6_out), .CLK_IN(clock_1_out),
    .INST_ID_IN(reorderbuffer_1_inst_id_out), .CBD1_IN(forwardingunit_1_cbd1),
    .CBD2_IN(forwardingunit_1_cbd2), .CBD3_IN(execute_1_cdbout3lsu), .RST(button_1_out),
    .CDBOUT3LSU(execute_1_cdbout3lsu), .CBDOUT1(execute_1_cbdout1), .CDBOUT2(execute_1_cdbout2));  // open: MEMORY_IN, MEMORY_OUT

  // Notes on the sheet:
  //   contents of rom_1 (hex, n*v repeats v):
  //   0 401000ff 40200001 4030000a 21423000
endmodule

module DecodeIssue (
  input  CLK_IN,
  input  [31:0] INST_IN,
  output [7:0] DECODE_OP,
  output [3:0] DECODE_DEST,
  output [3:0] DECODE_QJ,
  output [3:0] DECODE_QK,
  output [15:0] DECODE_CONST
);

  Pull_Resistor pull_resistor_1 (.node(INST_IN[31:24]));
  Pull_Resistor pull_resistor_2 (.node(INST_IN[23:20]));
  Pull_Resistor pull_resistor_3 (.node(INST_IN[15:0]));
  Pull_Resistor pull_resistor_4 (.node(INST_IN[19:16]));
  Pull_Resistor pull_resistor_5 (.node(INST_IN[15:12]));

  assign DECODE_CONST = INST_IN[15:0];
  assign DECODE_DEST = INST_IN[23:20];
  assign DECODE_OP = INST_IN[31:24];
  assign DECODE_QJ = INST_IN[19:16];
  assign DECODE_QK = INST_IN[15:12];
endmodule

module Execute (
  input  [7:0] Ex_OPIN,
  input  [7:0] EX_DESTIN,
  input  [7:0] EX_QJIN,
  input  [7:0] EX_QKIN,
  input  [31:0] EX_CONST_IN,
  input  CLK_IN,
  input  [3:0] INST_ID_IN,
  input  [31:0] MEMORY_IN,
  input  [39:0] CBD1_IN,
  input  [39:0] CBD2_IN,
  input  [39:0] CBD3_IN,
  input  RST,
  output [39:0] CDBOUT3LSU,
  output [39:0] CBDOUT1,
  output [39:0] CDBOUT2,
  output [63:0] MEMORY_OUT
);

  wire and_1_out, and_2_out, demultiplexer_1_out0, demultiplexer_1_out1, loadstoreunit_1_funit_empty,
       or_1_out, priority_encoder_1_p3, priority_encoder_1_p4, pull_resistor_1_node, pull_resistor_2_node,
       reservationstation_1_loadunit;
  wire [7:0] reservationstation_1_dest, reservationstation_1_op;
  wire [31:0] reservationstation_1_aout, reservationstation_1_bout;

  ReservationStation reservationstation_1 (
    .OPIN(Ex_OPIN), .DESTIN(EX_DESTIN), .QJIN(EX_QJIN), .QKIN(EX_QKIN), .CLKIN(CLK_IN), .CBDIN1(CBD1_IN),
    .CBDIN2(CBD2_IN), .CBDIN3(CBD3_IN), .RS_CONST_IN(EX_CONST_IN), .INST_ID(INST_ID_IN),
    .Unit_loaded_instruction(pull_resistor_1_node), .RST(RST), .LoadUnit(reservationstation_1_loadunit),
    .OP(reservationstation_1_op), .DEST(reservationstation_1_dest), .AOUT(reservationstation_1_aout),
    .BOUT(reservationstation_1_bout));  // open: INST_ID_OUT
  Pull_Resistor pull_resistor_1 (.node(pull_resistor_1_node));
  or or_1 (or_1_out, reservationstation_1_op[6], reservationstation_1_op[5]);
  and and_1 (and_1_out, reservationstation_1_loadunit, or_1_out);
  Demultiplexer demultiplexer_1 (
    .out0(demultiplexer_1_out0), .out1(demultiplexer_1_out1), .in(and_1_out), .sel(pull_resistor_2_node));
  and and_2 (and_2_out, reservationstation_1_op[7], loadstoreunit_1_funit_empty, reservationstation_1_loadunit);
  Pull_Resistor pull_resistor_2 (.node(pull_resistor_2_node));
  // Priority_Encoder #(.select(1)) priority_encoder_1: pin names not known; wires that end beside it: pull_resistor_2_node, 1'b1, priority_encoder_1_p3, priority_encoder_1_p4
  or or_2 (pull_resistor_1_node, demultiplexer_1_out1, demultiplexer_1_out0, and_2_out);
  LoadStoreUnit loadstoreunit_1 (
    .OP_IN(reservationstation_1_op), .ADDRESS_IN(reservationstation_1_aout),
    .DATA_IN(reservationstation_1_bout), .DEST_IN(reservationstation_1_dest), .LOAD_UNIT(and_2_out),
    .CLK_IN(CLK_IN), .FROM_MEM_BUFFER(MEMORY_IN), .CLEAR(RST), .CDB_OUT(CDBOUT3LSU),
    .TO_MEM_BUFFER(MEMORY_OUT), .FUNIT_EMPTY(loadstoreunit_1_funit_empty));  // open: FUNIT_RUNNING, FUNIT_READY
  IntegerFunctionalUnit integerfunctionalunit_1 (
    .OP_IN(reservationstation_1_op), .A_IN(reservationstation_1_aout), .B_IN(reservationstation_1_bout),
    .DEST_IN(reservationstation_1_dest), .LOAD_UNIT(demultiplexer_1_out0), .CLK_IN(CLK_IN), .CLEAR(RST),
    .CDB_OUT(CBDOUT1), .FUNIT_EMPTY(priority_encoder_1_p3));  // open: FUNIT_RUNNING, FUNIT_READY
  IntegerFunctionalUnit integerfunctionalunit_2 (
    .OP_IN(reservationstation_1_op), .A_IN(reservationstation_1_aout), .B_IN(reservationstation_1_bout),
    .DEST_IN(reservationstation_1_dest), .LOAD_UNIT(demultiplexer_1_out1), .CLK_IN(CLK_IN), .CLEAR(RST),
    .CDB_OUT(CDBOUT2), .FUNIT_EMPTY(priority_encoder_1_p4));  // open: FUNIT_RUNNING, FUNIT_READY
  Pull_Resistor pull_resistor_3 (.node(CDBOUT3LSU));
  Pull_Resistor pull_resistor_4 (.node(CBDOUT1));
  Pull_Resistor pull_resistor_5 (.node(CDBOUT2));

  // Notes on the sheet:
  //   INST_ID_IN: pull=down
  //   CBD1_IN: pull=down
  //   CBD2_IN: pull=down
  //   CBD3_IN: pull=down
endmodule

module InstructionFetch (
  input  RST,
  input  CLK_IN,
  input  [31:0] JUMP_ADRESS,
  input  LOAD_ADRESS,
  input  LOAD_NEXT,
  input  [31:0] DATA_IN,
  output [31:0] INST_OUT,
  output [31:0] NEXT_ADRESS
);

  wire and_1_out, and_2_out, not_1_out, or_1_out;

  and and_1 (and_1_out, LOAD_ADRESS, CLK_IN);
  and and_2 (and_2_out, CLK_IN, LOAD_NEXT);
  not not_1 (not_1_out, LOAD_ADRESS);
  or or_1 (or_1_out, and_1_out, and_2_out);
  Counter #(.max('hffffffff), .width(32)) counter_1 (
    .clr(RST), .load(LOAD_ADRESS), .up(1'b1), .count(not_1_out), .clk(or_1_out), .D(JUMP_ADRESS),
    .Q(NEXT_ADRESS));  // open: carry
  Multiplexer #(.width(32)) multiplexer_1 (.in0({32{1'b0}}), .in1(DATA_IN), .out(INST_OUT), .sel(LOAD_NEXT));
  Pull_Resistor pull_resistor_1 (.node(INST_OUT));

  // Notes on the sheet:
  //   INST_OUT: pull=down
  //   JUMP_ADRESS: pull=down
  //   LOAD_ADRESS: pull=down
  //   LOAD_NEXT: pull=down
endmodule

module ArchitecturalRegisterFile (
  input  [31:0] ARF_Data,
  input  [3:0] ARF_A_Sel,
  input  [3:0] ARF_B_Sel,
  input  [3:0] ARF_Write_Sel,
  input  ARF_Write,
  input  ARF_Clk,
  input  RESET,
  output [31:0] ARF_A,
  output [31:0] ARF_B,
  output WRITTEN
);

  wire comparator_1_eq, comparator_2_eq, demultiplexer_1_out1, demultiplexer_1_out2, demultiplexer_1_out3,
       demultiplexer_1_out4, demultiplexer_1_out5, demultiplexer_1_out6, demultiplexer_1_out7,
       demultiplexer_1_out8, demultiplexer_1_out9, demultiplexer_1_out10, demultiplexer_1_out11,
       demultiplexer_1_out12, demultiplexer_1_out13, demultiplexer_1_out14, demultiplexer_1_out15, not_1_out;
  wire [31:0] multiplexer_3_out, R1_q, R2_q, R3_q, R4_q, R5_q, R6_q, R7_q, R8_q, R9_q, R10_q, R11_q, R12_q,
       R13_q, R14_q, R15_q;

  Demultiplexer #(.select(4)) demultiplexer_1 (
    .out1(demultiplexer_1_out1), .out2(demultiplexer_1_out2), .out3(demultiplexer_1_out3),
    .out4(demultiplexer_1_out4), .out5(demultiplexer_1_out5), .out6(demultiplexer_1_out6),
    .out7(demultiplexer_1_out7), .out8(demultiplexer_1_out8), .out9(demultiplexer_1_out9),
    .out10(demultiplexer_1_out10), .out11(demultiplexer_1_out11), .out12(demultiplexer_1_out12),
    .out13(demultiplexer_1_out13), .out14(demultiplexer_1_out14), .out15(demultiplexer_1_out15),
    .in(ARF_Write), .sel(ARF_Write_Sel));  // open: out0
  Register #(.width(32)) R1 (.D(ARF_Data), .en(demultiplexer_1_out1), .clk(ARF_Clk), .Q(R1_q), .clr(RESET));
  Register #(.width(32)) R2 (.D(ARF_Data), .en(demultiplexer_1_out2), .clk(ARF_Clk), .Q(R2_q), .clr(RESET));
  Register #(.width(32)) R3 (.D(ARF_Data), .en(demultiplexer_1_out3), .clk(ARF_Clk), .Q(R3_q), .clr(RESET));
  Register #(.width(32)) R4 (.D(ARF_Data), .en(demultiplexer_1_out4), .clk(ARF_Clk), .Q(R4_q), .clr(RESET));
  Register #(.width(32)) R5 (.D(ARF_Data), .en(demultiplexer_1_out5), .clk(ARF_Clk), .Q(R5_q), .clr(RESET));
  Register #(.width(32)) R6 (.D(ARF_Data), .en(demultiplexer_1_out6), .clk(ARF_Clk), .Q(R6_q), .clr(RESET));
  Register #(.width(32)) R7 (.D(ARF_Data), .en(demultiplexer_1_out7), .clk(ARF_Clk), .Q(R7_q), .clr(RESET));
  Register #(.width(32)) R8 (.D(ARF_Data), .en(demultiplexer_1_out8), .clk(ARF_Clk), .Q(R8_q), .clr(RESET));
  Register #(.width(32)) R9 (.D(ARF_Data), .en(demultiplexer_1_out9), .clk(ARF_Clk), .Q(R9_q), .clr(RESET));
  Register #(.width(32)) R10 (.D(ARF_Data), .en(demultiplexer_1_out10), .clk(ARF_Clk), .Q(R10_q), .clr(RESET));
  Register #(.width(32)) R11 (.D(ARF_Data), .en(demultiplexer_1_out11), .clk(ARF_Clk), .Q(R11_q), .clr(RESET));
  Register #(.width(32)) R12 (.D(ARF_Data), .en(demultiplexer_1_out12), .clk(ARF_Clk), .Q(R12_q), .clr(RESET));
  Register #(.width(32)) R13 (.D(ARF_Data), .en(demultiplexer_1_out13), .clk(ARF_Clk), .Q(R13_q), .clr(RESET));
  Register #(.width(32)) R14 (.D(ARF_Data), .en(demultiplexer_1_out14), .clk(ARF_Clk), .Q(R14_q), .clr(RESET));
  Register #(.width(32)) R15 (.D(ARF_Data), .en(demultiplexer_1_out15), .clk(ARF_Clk), .Q(R15_q), .clr(RESET));
  Multiplexer #(.select(4), .width(32)) multiplexer_1 (
    .in0({32{1'b0}}), .in1(R1_q), .in2(R2_q), .in3(R3_q), .in4(R4_q), .in5(R5_q), .in6(R6_q), .in7(R7_q),
    .in8(R8_q), .in9(R9_q), .in10(R10_q), .in11(R11_q), .in12(R12_q), .in13(R13_q), .in14(R14_q),
    .in15(R15_q), .out(ARF_A), .sel(ARF_A_Sel));
  Multiplexer #(.select(4), .width(32)) multiplexer_2 (
    .in0({32{1'b0}}), .in1(R1_q), .in2(R2_q), .in3(R3_q), .in4(R4_q), .in5(R5_q), .in6(R6_q), .in7(R7_q),
    .in8(R8_q), .in9(R9_q), .in10(R10_q), .in11(R11_q), .in12(R12_q), .in13(R13_q), .in14(R14_q),
    .in15(R15_q), .out(ARF_B), .sel(ARF_B_Sel));
  Multiplexer #(.select(4), .width(32)) multiplexer_3 (
    .in0({32{1'b0}}), .in1(R1_q), .in2(R2_q), .in3(R3_q), .in4(R4_q), .in5(R5_q), .in6(R6_q), .in7(R7_q),
    .in8(R8_q), .in9(R9_q), .in10(R10_q), .in11(R11_q), .in12(R12_q), .in13(R13_q), .in14(R14_q),
    .in15(R15_q), .out(multiplexer_3_out), .sel(ARF_Write_Sel));
  Comparator #(.width(32)) comparator_1 (.a(multiplexer_3_out), .b(ARF_Data), .eq(comparator_1_eq));  // open: gt, lt
  not not_1 (not_1_out, comparator_2_eq);
  Comparator #(.width(32)) comparator_2 (.a(ARF_Data), .b({32{1'b0}}), .eq(comparator_2_eq));  // open: gt, lt
  and and_1 (WRITTEN, comparator_1_eq, not_1_out);

  // Notes on the sheet:
  //   ARF_A: pull=down
  //   ARF_B: pull=down
  //   WRITTEN: pull=down
  //   ARF_Data: pull=down
  //   ARF_A_Sel: pull=down
  //   ARF_B_Sel: pull=down
  //   ARF_Write_Sel: pull=down
  //   ARF_Write: pull=down
  //   ARF_Clk: pull=down
endmodule

module ReservationStation (
  input  [7:0] OPIN,
  input  [7:0] DESTIN,
  input  [7:0] QJIN,
  input  [7:0] QKIN,
  input  CLKIN,
  input  [39:0] CBDIN1,
  input  [39:0] CBDIN2,
  input  [39:0] CBDIN3,
  input  [31:0] RS_CONST_IN,
  input  [3:0] INST_ID,
  input  Unit_loaded_instruction,
  input  RST,
  output LoadUnit,
  output [7:0] OP,
  output [7:0] DEST,
  output [31:0] AOUT,
  output [31:0] BOUT,
  output [3:0] INST_ID_OUT
);

  wire and_2_out, buffer_1_out, buffer_2_out, buffer_3_out, buffer_4_out, buffer_5_out, demultiplexer_1_out0,
       demultiplexer_1_out1, demultiplexer_1_out2, demultiplexer_1_out3, demultiplexer_2_out0,
       demultiplexer_2_out1, demultiplexer_2_out2, demultiplexer_2_out3, not_1_out, or_1_out, or_2_out,
       or_3_out, or_4_out, priority_encoder_1_gs, priority_encoder_2_gs, register_3_q,
       reservationstationline_1_isfree, reservationstationline_1_ready, reservationstationline_2_isfree,
       reservationstationline_2_ready, reservationstationline_3_isfree, reservationstationline_3_ready,
       reservationstationline_4_isfree, reservationstationline_4_ready;
  wire [2:0] priority_encoder_1_out, pull_resistor_8_node, register_1_q, register_2_q;
  wire [3:0] reservationstationline_1_inst_id_out, reservationstationline_2_inst_id_out,
       reservationstationline_3_inst_id_out, reservationstationline_4_inst_id_out;
  wire [7:0] reservationstationline_1_dest_out, reservationstationline_1_op_out,
       reservationstationline_2_dest_out, reservationstationline_2_op_out, reservationstationline_3_dest_out,
       reservationstationline_3_op_out, reservationstationline_4_dest_out, reservationstationline_4_op_out;
  wire [31:0] reservationstationline_1_a_out, reservationstationline_1_b_out, reservationstationline_2_a_out,
       reservationstationline_2_b_out, reservationstationline_3_a_out, reservationstationline_3_b_out,
       reservationstationline_4_a_out, reservationstationline_4_b_out;

  Demultiplexer #(.select(3)) demultiplexer_1 (
    .out0(demultiplexer_1_out0), .out1(demultiplexer_1_out1), .out2(demultiplexer_1_out2),
    .out3(demultiplexer_1_out3), .in(register_3_q), .sel(register_2_q));  // open: out4, out5, out6, out7
  Pull_Resistor pull_resistor_1 (.node(CLKIN));
  Pull_Resistor pull_resistor_2 (.node(CBDIN1));
  Pull_Resistor pull_resistor_3 (.node(CBDIN2));
  Demultiplexer #(.select(3)) demultiplexer_2 (
    .out0(demultiplexer_2_out0), .out1(demultiplexer_2_out1), .out2(demultiplexer_2_out2),
    .out3(demultiplexer_2_out3), .in(buffer_1_out), .sel(priority_encoder_1_out));  // open: out4, out5, out6, out7
  buf buffer_1 (buffer_1_out, buffer_2_out);
  buf buffer_2 (buffer_2_out, buffer_3_out);
  Pull_Resistor pull_resistor_4 (.node(CBDIN3));
  buf buffer_3 (buffer_3_out, buffer_4_out);
  buf buffer_4 (buffer_4_out, buffer_5_out);
  buf buffer_5 (buffer_5_out, Unit_loaded_instruction);
  or or_1 (or_1_out, demultiplexer_2_out0, RST);
  or or_2 (or_2_out, demultiplexer_2_out1, RST);
  or or_3 (or_3_out, demultiplexer_2_out2, RST);
  or or_4 (or_4_out, demultiplexer_2_out3, RST);
  ReservationStationLine reservationstationline_1 (
    .CBDIN1(CBDIN1), .CBDIN2(CBDIN2), .CBDIN3(CBDIN3), .OP_IN(OPIN), .Dest_IN(DESTIN), .QJ_IN(QJIN),
    .QK_IN(QKIN), .CLEAR(or_1_out), .CLK_IN(CLKIN), .Write(demultiplexer_1_out0), .CONST_IN(RS_CONST_IN),
    .INST_ID(INST_ID), .Ready(reservationstationline_1_ready), .IsFree(reservationstationline_1_isfree),
    .Op_out(reservationstationline_1_op_out), .Dest_out(reservationstationline_1_dest_out),
    .A_out(reservationstationline_1_a_out), .B_out(reservationstationline_1_b_out),
    .INST_ID_OUT(reservationstationline_1_inst_id_out));
  ReservationStationLine reservationstationline_2 (
    .CBDIN1(CBDIN1), .CBDIN2(CBDIN2), .CBDIN3(CBDIN3), .OP_IN(OPIN), .Dest_IN(DESTIN), .QJ_IN(QJIN),
    .QK_IN(QKIN), .CLEAR(or_2_out), .CLK_IN(CLKIN), .Write(demultiplexer_1_out1), .CONST_IN(RS_CONST_IN),
    .INST_ID(INST_ID), .Ready(reservationstationline_2_ready), .IsFree(reservationstationline_2_isfree),
    .Op_out(reservationstationline_2_op_out), .Dest_out(reservationstationline_2_dest_out),
    .A_out(reservationstationline_2_a_out), .B_out(reservationstationline_2_b_out),
    .INST_ID_OUT(reservationstationline_2_inst_id_out));
  ReservationStationLine reservationstationline_3 (
    .CBDIN1(CBDIN1), .CBDIN2(CBDIN2), .CBDIN3(CBDIN3), .OP_IN(OPIN), .Dest_IN(DESTIN), .QJ_IN(QJIN),
    .QK_IN(QKIN), .CLEAR(or_3_out), .CLK_IN(CLKIN), .Write(demultiplexer_1_out2), .CONST_IN(RS_CONST_IN),
    .INST_ID(INST_ID), .Ready(reservationstationline_3_ready), .IsFree(reservationstationline_3_isfree),
    .Op_out(reservationstationline_3_op_out), .Dest_out(reservationstationline_3_dest_out),
    .A_out(reservationstationline_3_a_out), .B_out(reservationstationline_3_b_out),
    .INST_ID_OUT(reservationstationline_3_inst_id_out));
  ReservationStationLine reservationstationline_4 (
    .CBDIN1(CBDIN1), .CBDIN2(CBDIN2), .CBDIN3(CBDIN3), .OP_IN(OPIN), .Dest_IN(DESTIN), .QJ_IN(QJIN),
    .QK_IN(QKIN), .CLEAR(or_4_out), .CLK_IN(CLKIN), .Write(demultiplexer_1_out3), .CONST_IN(RS_CONST_IN),
    .INST_ID(INST_ID), .Ready(reservationstationline_4_ready), .IsFree(reservationstationline_4_isfree),
    .Op_out(reservationstationline_4_op_out), .Dest_out(reservationstationline_4_dest_out),
    .A_out(reservationstationline_4_a_out), .B_out(reservationstationline_4_b_out),
    .INST_ID_OUT(reservationstationline_4_inst_id_out));
  Priority_Encoder priority_encoder_1 (
    .in0(reservationstationline_1_ready), .in1(reservationstationline_2_ready),
    .in2(reservationstationline_3_ready), .in3(reservationstationline_4_ready), .out(priority_encoder_1_out),
    .gs(priority_encoder_1_gs));  // open: in4, in5, in6, in7, en_in, en_out
  Pull_Resistor pull_resistor_5 (.node(OP));
  Multiplexer #(.select(3), .width(8)) multiplexer_1 (
    .in0(reservationstationline_1_op_out), .in1(reservationstationline_2_op_out),
    .in2(reservationstationline_3_op_out), .in3(reservationstationline_4_op_out), .out(OP),
    .sel(priority_encoder_1_out));  // open: in4, in5, in6, in7
  Multiplexer #(.select(3), .width(8)) multiplexer_2 (
    .in0(reservationstationline_1_dest_out), .in1(reservationstationline_2_dest_out),
    .in2(reservationstationline_3_dest_out), .in3(reservationstationline_4_dest_out), .out(DEST),
    .sel(priority_encoder_1_out));  // open: in4, in5, in6, in7
  Multiplexer #(.select(3), .width(32)) multiplexer_3 (
    .in0(reservationstationline_1_a_out), .in1(reservationstationline_2_a_out),
    .in2(reservationstationline_3_a_out), .in3(reservationstationline_4_a_out), .out(AOUT),
    .sel(priority_encoder_1_out));  // open: in4, in5, in6, in7
  Multiplexer #(.select(3), .width(32)) multiplexer_4 (
    .in0(reservationstationline_1_b_out), .in1(reservationstationline_2_b_out),
    .in2(reservationstationline_3_b_out), .in3(reservationstationline_4_b_out), .out(BOUT),
    .sel(priority_encoder_1_out));  // open: in4, in5, in6, in7
  Multiplexer #(.select(3), .width(4)) multiplexer_5 (
    .in0(reservationstationline_1_inst_id_out), .in1(reservationstationline_2_inst_id_out),
    .in2(reservationstationline_3_inst_id_out), .in3(reservationstationline_4_inst_id_out),
    .out(INST_ID_OUT), .sel(priority_encoder_1_out));  // open: in4, in5, in6, in7
  Register #(.width(3)) register_1 (.D(priority_encoder_1_out), .en(CLKIN), .clk(CLKIN), .Q(register_1_q), .clr(RST));
  Pull_Resistor pull_resistor_6 (.node(priority_encoder_1_out));
  and and_1 (LoadUnit, priority_encoder_1_gs, CLKIN);
  Pull_Resistor pull_resistor_7 (.node(register_1_q));
  Pull_Resistor pull_resistor_8 (.node(pull_resistor_8_node));
  Priority_Encoder priority_encoder_2 (
    .in0(reservationstationline_1_isfree), .in1(reservationstationline_2_isfree),
    .in2(reservationstationline_3_isfree), .in3(reservationstationline_4_isfree), .out(pull_resistor_8_node),
    .gs(priority_encoder_2_gs));  // open: in4, in5, in6, in7, en_in, en_out
  and and_2 (and_2_out, priority_encoder_2_gs, CLKIN);
  Pull_Resistor pull_resistor_9 (.node(LoadUnit));
  Pull_Resistor pull_resistor_10 (.node(OP));
  Pull_Resistor pull_resistor_11 (.node(DEST));
  Pull_Resistor pull_resistor_12 (.node(AOUT));
  Pull_Resistor pull_resistor_13 (.node(BOUT));
  Pull_Resistor pull_resistor_14 (.node(INST_ID_OUT));
  Register #(.width(3)) register_2 (.D(pull_resistor_8_node), .en(CLKIN), .clk(CLKIN), .Q(register_2_q), .clr(RST));
  Register #(.trigger("high"), .width(1)) register_3 (
    .D(and_2_out), .en(CLKIN), .clk(CLKIN), .Q(register_3_q), .clr(not_1_out));
  not not_1 (not_1_out, CLKIN);
  Pull_Resistor pull_resistor_15 (.node(register_2_q));

  // Notes on the sheet:
  //   Unit_loaded_instruction: pull=down
endmodule

module ReservationStationLine (
  input  [39:0] CBDIN1,
  input  [39:0] CBDIN2,
  input  [39:0] CBDIN3,
  input  [7:0] OP_IN,
  input  [7:0] Dest_IN,
  input  [7:0] QJ_IN,
  input  [7:0] QK_IN,
  input  CLEAR,
  input  CLK_IN,
  input  Write,
  input  [31:0] CONST_IN,
  input  [3:0] INST_ID,
  output Ready,
  output IsFree,
  output [7:0] Op_out,
  output [7:0] Dest_out,
  output [31:0] A_out,
  output [31:0] B_out,
  output [3:0] INST_ID_OUT
);

  wire and_1_out, buffer_1_out, buffer_2_out, buffer_3_out, comparator_1_eq, comparator_2_eq,
       comparator_3_eq, comparator_5_eq, comparator_6_eq, comparator_7_eq, comparator_8_eq, comparator_9_eq,
       comparator_10_eq, not_1_out, not_2_out, or_1_out, priority_encoder_1_p5, priority_encoder_2_p4;
  wire [1:0] priority_encoder_1_p3, priority_encoder_2_p2;
  wire [7:0] QJ_q, QK_q;
  wire [31:0] multiplexer_1_out, multiplexer_2_out, register_3_q, VJ_q;

  buf buffer_1 (buffer_1_out, CLK_IN);
  buf buffer_2 (buffer_2_out, buffer_1_out);
  buf buffer_3 (buffer_3_out, buffer_2_out);
  Comparator comparator_1 (.a(CBDIN1[39:32]), .b(QJ_q), .eq(comparator_1_eq));  // open: gt, lt
  Comparator comparator_2 (.a(CBDIN2[39:32]), .b(QJ_q), .eq(comparator_2_eq));  // open: gt, lt
  Comparator comparator_3 (.a(CBDIN3[39:32]), .b(QJ_q), .eq(comparator_3_eq));  // open: gt, lt
  Register register_1 (.D(OP_IN), .en(Write), .clk(Write), .Q(Op_out), .clr(CLEAR));
  Register #(.width(4)) register_2 (.D(INST_ID), .en(Write), .clk(Write), .Q(INST_ID_OUT), .clr(CLEAR));
  Pull_Resistor pull_resistor_1 (.node(comparator_1_eq));
  Pull_Resistor pull_resistor_2 (.node(comparator_2_eq));
  Pull_Resistor pull_resistor_3 (.node(comparator_3_eq));
  Register Dest (.D(Dest_IN), .en(Write), .clk(Write), .Q(Dest_out), .clr(CLEAR));
  Comparator comparator_4 (.a(Op_out), .b({8{1'b0}}), .eq(IsFree));  // open: gt, lt
  // Priority_Encoder #(.select(2)) priority_encoder_1: pin names not known; wires that end beside it: comparator_3_eq, comparator_2_eq, priority_encoder_1_p3, comparator_1_eq, priority_encoder_1_p5
  Comparator comparator_5 (.a(Op_out), .b(8'h40), .eq(comparator_5_eq));  // open: gt, lt
  Multiplexer #(.select(2), .width(32)) multiplexer_1 (
    .in0(CBDIN3[31:0]), .in1(CBDIN2[31:0]), .in2(CBDIN1[31:0]), .out(multiplexer_1_out),
    .sel(priority_encoder_1_p3));  // open: in3
  Register QJ (.D(QJ_IN), .en(Write), .clk(Write), .Q(QJ_q), .clr(CLEAR));
  Register QK (.D(QK_IN), .en(Write), .clk(Write), .Q(QK_q), .clr(CLEAR));
  Comparator comparator_6 (.a(CBDIN1[39:32]), .b(QK_q), .eq(comparator_6_eq));  // open: gt, lt
  Comparator comparator_7 (.a(CBDIN2[39:32]), .b(QK_q), .eq(comparator_7_eq));  // open: gt, lt
  Comparator comparator_8 (.a(CBDIN3[39:32]), .b(QK_q), .eq(comparator_8_eq));  // open: gt, lt
  or or_1 (or_1_out, CLEAR, Write);
  Register #(.width(32)) register_3 (.D(CONST_IN), .en(Write), .clk(Write), .Q(register_3_q));  // open: clr
  // Priority_Encoder #(.select(2)) priority_encoder_2: pin names not known; wires that end beside it: comparator_8_eq, priority_encoder_2_p2, comparator_7_eq, priority_encoder_2_p4, comparator_6_eq
  Multiplexer #(.select(2), .width(32)) multiplexer_2 (
    .in1(CBDIN3[31:0]), .in2(CBDIN2[31:0]), .in3(CBDIN1[31:0]), .out(multiplexer_2_out),
    .sel(priority_encoder_2_p2));  // open: in0
  Register #(.width(32)) VJ (
    .D(multiplexer_1_out), .en(priority_encoder_1_p5), .clk(buffer_3_out), .Q(VJ_q), .clr(or_1_out));
  Register #(.width(32)) VK (
    .D(multiplexer_2_out), .en(priority_encoder_2_p4), .clk(buffer_3_out), .Q(B_out), .clr(or_1_out));
  Comparator #(.width(32)) comparator_9 (.a(B_out), .b({32{1'b0}}), .eq(comparator_9_eq));  // open: gt, lt
  not not_1 (not_1_out, comparator_9_eq);
  not not_2 (not_2_out, comparator_10_eq);
  Comparator #(.width(32)) comparator_10 (.a(VJ_q), .b({32{1'b0}}), .eq(comparator_10_eq));  // open: gt, lt
  Multiplexer #(.width(32)) multiplexer_3 (.in0(VJ_q), .in1(register_3_q), .out(A_out), .sel(comparator_5_eq));
  and and_1 (and_1_out, not_1_out, not_2_out);
  or or_2 (Ready, and_1_out, comparator_5_eq);
endmodule

module IntegerFunctionalUnit (
  input  [7:0] OP_IN,
  input  [31:0] A_IN,
  input  [31:0] B_IN,
  input  [7:0] DEST_IN,
  input  LOAD_UNIT,
  input  CLK_IN,
  input  CLEAR,
  output FUNIT_RUNNING,
  output [39:0] CDB_OUT,
  output FUNIT_READY,
  output FUNIT_EMPTY
);

  wire comparator_1_eq, comparator_2_gt, comparator_3_eq, not_1_out, not_2_out, not_3_out, or_1_out;
  wire [4:0] bit_extender_1_out, bit_extender_2_out, bit_extender_3_out;
  wire [7:0] register_2_q;
  wire [31:0] adder_1_out, divider_1_out, multiplexer_1_out, multiplier_1_out, register_3_q, register_4_q,
       shifter_1_out, shifter_2_out, shifter_3_out, subtractor_1_out;

  Register register_1 (.D(DEST_IN), .en(LOAD_UNIT), .clk(LOAD_UNIT), .Q(CDB_OUT[39:32]), .clr(CLEAR));
  Register register_2 (.D(OP_IN), .en(LOAD_UNIT), .clk(LOAD_UNIT), .Q(register_2_q), .clr(CLEAR));
  Register #(.width(32)) register_3 (.D(A_IN), .en(LOAD_UNIT), .clk(LOAD_UNIT), .Q(register_3_q), .clr(CLEAR));
  Register #(.width(32)) register_4 (.D(B_IN), .en(LOAD_UNIT), .clk(LOAD_UNIT), .Q(register_4_q), .clr(CLEAR));
  Comparator comparator_1 (.a(register_2_q), .b(8'h40), .eq(comparator_1_eq));  // open: gt, lt
  Comparator comparator_2 (.a(register_2_q), .b({8{1'b0}}), .gt(comparator_2_gt));  // open: eq, lt
  or or_1 (or_1_out, LOAD_UNIT, CLEAR);
  Comparator #(.width(4)) comparator_3 (.a(register_2_q[7:4]), .b(4'b0010), .eq(comparator_3_eq));  // open: gt, lt
  Adder #(.width(32)) adder_1 (.a(register_3_q), .b(register_4_q), .out(adder_1_out));  // open: cin, cout
  Subtractor #(.width(32)) subtractor_1 (
    .a(register_3_q), .b(register_4_q), .out(subtractor_1_out));  // open: bin, bout
  Multiplier #(.width(32)) multiplier_1 (
    .a(register_3_q), .b(register_4_q), .out(multiplier_1_out));  // open: cin, cout
  Divider #(.width(32)) divider_1 (.a(register_3_q), .b(register_4_q), .out(divider_1_out));  // open: upper, rem
  Shifter #(.width(32)) shifter_1 (.in(register_3_q), .\dist (bit_extender_1_out), .out(shifter_1_out));
  Bit_Extender #(.in_width(32), .out_width(5)) bit_extender_1 (.in(register_4_q), .out(bit_extender_1_out));
  Shifter #(.shift("lr"), .width(32)) shifter_2 (.in(register_3_q), .\dist (bit_extender_2_out), .out(shifter_2_out));
  Bit_Extender #(.in_width(32), .out_width(5)) bit_extender_2 (.in(register_4_q), .out(bit_extender_2_out));
  Shifter #(.shift("ar"), .width(32)) shifter_3 (.in(register_3_q), .\dist (bit_extender_3_out), .out(shifter_3_out));
  Bit_Extender #(.in_width(32), .out_width(5)) bit_extender_3 (.in(register_4_q), .out(bit_extender_3_out));
  Multiplexer #(.enable("true"), .select(4), .width(32)) multiplexer_1 (
    .in0(register_3_q), .in1(adder_1_out), .in2(subtractor_1_out), .in3(multiplier_1_out),
    .in4(divider_1_out), .in5(shifter_1_out), .in6(shifter_2_out), .in7(shifter_3_out),
    .out(multiplexer_1_out), .sel(register_2_q[3:0]), .en(comparator_3_eq));  // open: in8, in9, in10, in11, in12, in13, in14, in15
  Multiplexer #(.width(32)) multiplexer_2 (
    .in0(multiplexer_1_out), .in1(register_3_q), .out(CDB_OUT[31:0]), .sel(comparator_1_eq));
  and and_1 (FUNIT_RUNNING, comparator_2_gt, not_1_out);
  not not_1 (not_1_out, FUNIT_READY);
  Counter #(.max('h4), .width(3)) counter_1 (
    .carry(FUNIT_READY), .clk(CLK_IN), .clr(or_1_out));  // open: load, D, count, Q, up
  Pull_Resistor pull_resistor_1 (.node(FUNIT_RUNNING));
  Pull_Resistor pull_resistor_2 (.node(CDB_OUT));
  Pull_Resistor pull_resistor_3 (.node(FUNIT_READY));
  not not_2 (not_2_out, FUNIT_RUNNING);
  and and_2 (FUNIT_EMPTY, not_2_out, not_3_out);
  not not_3 (not_3_out, FUNIT_READY);

  // Notes on the sheet:
  //   FUNIT_READY: pull=down
  //   FUNIT_EMPTY: pull=down
  //   CLK_IN: pull=down
endmodule

module LoadStoreUnit (
  input  [7:0] OP_IN,
  input  [31:0] ADDRESS_IN,
  input  [31:0] DATA_IN,
  input  [7:0] DEST_IN,
  input  LOAD_UNIT,
  input  CLK_IN,
  input  [31:0] FROM_MEM_BUFFER,
  input  CLEAR,
  output FUNIT_RUNNING,
  output [39:0] CDB_OUT,
  output [63:0] TO_MEM_BUFFER,
  output FUNIT_READY,
  output FUNIT_EMPTY
);

  Pull_Resistor pull_resistor_1 (.node(FUNIT_RUNNING));
  Pull_Resistor pull_resistor_2 (.node(CDB_OUT));
  Pull_Resistor pull_resistor_3 (.node(TO_MEM_BUFFER));
  Pull_Resistor pull_resistor_4 (.node(FUNIT_READY));
  Pull_Resistor pull_resistor_5 (.node(FUNIT_EMPTY));
  Pull_Resistor pull_resistor_6 ();  // open: node

  // Notes on the sheet:
  //   TO_MEM_BUFFER: pull=down
  //   FUNIT_READY: pull=down
  //   FUNIT_EMPTY: pull=down
  //   CLK_IN: pull=down
  //   FROM_MEM_BUFFER: pull=down
  //   CLEAR: pull=down
endmodule

module ReorderBuffer (
  input  CLK_IN,
  input  [7:0] OP_IN,
  input  [7:0] DEST,
  input  RESET,
  input  [39:0] CBD1_IN,
  input  [39:0] CBD2_IN,
  input  [39:0] CBD3_IN,
  input  WRITTEN_CONFIRM,
  output ENTRY_AVAILABLE,
  output READY,
  output [3:0] INST_ID_OUT,
  output [7:0] ROB_DEST,
  output [31:0] ROB_RESULT
);

  wire and_1_out, and_2_out, and_3_out, and_4_out, comparator_1_eq, comparator_2_eq, comparator_3_eq,
       Head_carry, not_1_out, not_2_out, not_3_out, or_1_out;
  wire [2:0] Tail_q;
  wire [3:0] reorderbufferentry_1_idxout, reorderbufferentry_2_idxout, reorderbufferentry_3_idxout,
       reorderbufferentry_4_idxout, reorderbufferentry_5_idxout, reorderbufferentry_6_idxout,
       reorderbufferentry_7_idxout;
  wire [19:0] pull_resistor_3_node;
  wire [31:0] pull_resistor_1_node;
  wire [43:40] Head_q;
  wire [63:0] reorderbufferentry_1_entry_out, reorderbufferentry_2_entry_out, reorderbufferentry_3_entry_out,
       reorderbufferentry_4_entry_out, reorderbufferentry_5_entry_out, reorderbufferentry_6_entry_out,
       reorderbufferentry_7_entry_out, reorderbufferentry_8_entry_out;
  wire [63:40] multiplexer_1_out;

  not not_1 (not_1_out, comparator_1_eq);
  Comparator comparator_1 (.a({8{1'b0}}), .b(OP_IN), .eq(comparator_1_eq));  // open: gt, lt
  not not_2 (not_2_out, comparator_2_eq);
  Comparator comparator_2 (.a({8{1'b0}}), .b(DEST), .eq(comparator_2_eq));  // open: gt, lt
  Pull_Resistor pull_resistor_1 (.node(pull_resistor_1_node));
  Pull_Resistor pull_resistor_2 (.node(Head_q[43]));
  Pull_Resistor pull_resistor_3 (.node(pull_resistor_3_node));
  not not_3 (not_3_out, CLK_IN);
  and and_1 (and_1_out, not_3_out, not_2_out, not_2_out);
  and and_2 (and_2_out, CLK_IN, not_1_out, not_2_out);
  Counter #(.max('h7), .width(3)) Tail (
    .Q(Tail_q), .clk(WRITTEN_CONFIRM), .clr(or_1_out));  // open: load, D, count, carry, up
  or or_1 (or_1_out, RESET, and_3_out);
  and and_3 (and_3_out, WRITTEN_CONFIRM, and_4_out);
  Counter #(.max('h7), .width(3)) Head (
    .Q(Head_q[42:40]), .carry(Head_carry), .clk(and_1_out), .clr(or_1_out));  // open: load, D, count, up
  Comparator #(.width(3)) comparator_3 (.a(Head_q[42:40]), .b(Tail_q), .eq(comparator_3_eq));  // open: gt, lt
  not not_4 (ENTRY_AVAILABLE, Head_carry);
  and and_4 (and_4_out, Head_carry, comparator_3_eq);
  ReorderBufferEntry reorderbufferentry_1 (
    .RST(RESET), .ENTRY_IN({pull_resistor_3_node, Head_q, DEST, pull_resistor_1_node}), .CBD1(CBD1_IN),
    .CBD2(CBD2_IN), .CBD3(CBD3_IN), .CLK(CLK_IN), .WRITE(and_2_out), .Selected(Head_q[42:40]),
    .IDXIN(4'b0000), .ENTRY_OUT(reorderbufferentry_1_entry_out), .IDXOUT(reorderbufferentry_1_idxout));
  ReorderBufferEntry reorderbufferentry_2 (
    .RST(RESET), .ENTRY_IN({pull_resistor_3_node, Head_q, DEST, pull_resistor_1_node}), .CBD1(CBD1_IN),
    .CBD2(CBD2_IN), .CBD3(CBD3_IN), .CLK(CLK_IN), .WRITE(and_2_out), .Selected(Head_q[42:40]),
    .IDXIN(reorderbufferentry_1_idxout), .ENTRY_OUT(reorderbufferentry_2_entry_out),
    .IDXOUT(reorderbufferentry_2_idxout));
  ReorderBufferEntry reorderbufferentry_3 (
    .RST(RESET), .ENTRY_IN({pull_resistor_3_node, Head_q, DEST, pull_resistor_1_node}), .CBD1(CBD1_IN),
    .CBD2(CBD2_IN), .CBD3(CBD3_IN), .CLK(CLK_IN), .WRITE(and_2_out), .Selected(Head_q[42:40]),
    .IDXIN(reorderbufferentry_2_idxout), .ENTRY_OUT(reorderbufferentry_3_entry_out),
    .IDXOUT(reorderbufferentry_3_idxout));
  ReorderBufferEntry reorderbufferentry_4 (
    .RST(RESET), .ENTRY_IN({pull_resistor_3_node, Head_q, DEST, pull_resistor_1_node}), .CBD1(CBD1_IN),
    .CBD2(CBD2_IN), .CBD3(CBD3_IN), .CLK(CLK_IN), .WRITE(and_2_out), .Selected(Head_q[42:40]),
    .IDXIN(reorderbufferentry_3_idxout), .ENTRY_OUT(reorderbufferentry_4_entry_out),
    .IDXOUT(reorderbufferentry_4_idxout));
  ReorderBufferEntry reorderbufferentry_5 (
    .RST(RESET), .ENTRY_IN({pull_resistor_3_node, Head_q, DEST, pull_resistor_1_node}), .CBD1(CBD1_IN),
    .CBD2(CBD2_IN), .CBD3(CBD3_IN), .CLK(CLK_IN), .WRITE(and_2_out), .Selected(Head_q[42:40]),
    .IDXIN(reorderbufferentry_4_idxout), .ENTRY_OUT(reorderbufferentry_5_entry_out),
    .IDXOUT(reorderbufferentry_5_idxout));
  ReorderBufferEntry reorderbufferentry_6 (
    .RST(RESET), .ENTRY_IN({pull_resistor_3_node, Head_q, DEST, pull_resistor_1_node}), .CBD1(CBD1_IN),
    .CBD2(CBD2_IN), .CBD3(CBD3_IN), .CLK(CLK_IN), .WRITE(and_2_out), .Selected(Head_q[42:40]),
    .IDXIN(reorderbufferentry_5_idxout), .ENTRY_OUT(reorderbufferentry_6_entry_out),
    .IDXOUT(reorderbufferentry_6_idxout));
  ReorderBufferEntry reorderbufferentry_7 (
    .RST(RESET), .ENTRY_IN({pull_resistor_3_node, Head_q, DEST, pull_resistor_1_node}), .CBD1(CBD1_IN),
    .CBD2(CBD2_IN), .CBD3(CBD3_IN), .CLK(CLK_IN), .WRITE(and_2_out), .Selected(Head_q[42:40]),
    .IDXIN(reorderbufferentry_6_idxout), .ENTRY_OUT(reorderbufferentry_7_entry_out),
    .IDXOUT(reorderbufferentry_7_idxout));
  ReorderBufferEntry reorderbufferentry_8 (
    .RST(RESET), .ENTRY_IN({pull_resistor_3_node, Head_q, DEST, pull_resistor_1_node}), .CBD1(CBD1_IN),
    .CBD2(CBD2_IN), .CBD3(CBD3_IN), .CLK(CLK_IN), .WRITE(and_2_out), .Selected(Head_q[42:40]),
    .IDXIN(reorderbufferentry_7_idxout), .ENTRY_OUT(reorderbufferentry_8_entry_out));  // open: IDXOUT
  Multiplexer #(.select(3), .width(64)) multiplexer_1 (
    .in0(reorderbufferentry_1_entry_out), .in1(reorderbufferentry_2_entry_out),
    .in2(reorderbufferentry_3_entry_out), .in3(reorderbufferentry_4_entry_out),
    .in4(reorderbufferentry_5_entry_out), .in5(reorderbufferentry_6_entry_out),
    .in6(reorderbufferentry_7_entry_out), .in7(reorderbufferentry_8_entry_out),
    .out({multiplexer_1_out[63:44], READY, multiplexer_1_out[42:40], ROB_DEST, ROB_RESULT}), .sel(Tail_q));
  Pull_Resistor pull_resistor_4 (.node(ENTRY_AVAILABLE));
  Pull_Resistor pull_resistor_5 (.node(READY));
  assign INST_ID_OUT = {{1{multiplexer_1_out[42]}}, multiplexer_1_out[42:40]};  // Bit_Extender bit_extender_1

  // Notes on the sheet:
  //   INST_ID_OUT: pull=down
  //   ROB_DEST: pull=down
  //   ROB_RESULT: pull=down
endmodule

module ReorderBufferEntry (
  input  RST,
  input  [63:0] ENTRY_IN,
  input  [39:0] CBD1,
  input  [39:0] CBD2,
  input  [39:0] CBD3,
  input  CLK,
  input  WRITE,
  input  [2:0] Selected,
  input  [3:0] IDXIN,
  output [63:0] ENTRY_OUT,
  output [3:0] IDXOUT
);

  wire and_1_out, and_2_out, and_3_out, and_4_out, comparator_1_eq, comparator_2_eq, comparator_3_eq,
       comparator_4_eq, comparator_5_eq, comparator_6_eq, comparator_7_eq, not_1_out, not_2_out, not_3_out,
       not_4_out, or_1_out, priority_encoder_1_gs;
  wire [1:0] pull_resistor_1_node;
  wire [3:0] bit_extender_1_out;
  wire [31:0] multiplexer_2_out;
  wire [43:0] register_1_q;
  wire [63:0] multiplexer_1_out, pull_resistor_2_node;
  wire [63:32] register_1_q_2;

  assign bit_extender_1_out = {{1{Selected[2]}}, Selected};  // Bit_Extender bit_extender_1
  not not_1 (not_1_out, comparator_1_eq);
  Comparator comparator_1 (.a(ENTRY_IN[39:32]), .b({8{1'b0}}), .eq(comparator_1_eq));  // open: gt, lt
  Comparator #(.width(4)) comparator_2 (.a(bit_extender_1_out), .b(IDXIN), .eq(comparator_2_eq));  // open: gt, lt
  Multiplexer #(.width(64)) multiplexer_1 (.in0(ENTRY_IN), .in1(ENTRY_OUT), .out(multiplexer_1_out), .sel(not_2_out));
  not not_2 (not_2_out, and_1_out);
  and and_1 (and_1_out, WRITE, not_1_out, comparator_2_eq);
  or or_1 (or_1_out, and_1_out, and_4_out);
  Adder #(.width(4)) adder_1 (.a(IDXIN), .b(4'b0001), .out(IDXOUT));  // open: cin, cout
  Register #(.trigger("high"), .width(64)) register_1 (
    .D(multiplexer_1_out), .en(and_2_out), .clk(CLK),
    .Q({register_1_q_2[63:44], register_1_q[43], register_1_q_2[42:32], register_1_q[31:0]}), .clr(RST));
  and and_2 (and_2_out, or_1_out, not_3_out);
  Comparator #(.width(64)) comparator_3 (
    .a({register_1_q_2[63:44], register_1_q[43], register_1_q_2[42:32], register_1_q[31:0]}),
    .b(multiplexer_1_out), .eq(comparator_3_eq));  // open: gt, lt
  not not_3 (not_3_out, comparator_3_eq);
  Comparator comparator_4 (.a(register_1_q_2[39:32]), .b(CBD1[39:32]), .eq(comparator_4_eq));  // open: gt, lt
  Comparator comparator_5 (.a(register_1_q_2[39:32]), .b(CBD2[39:32]), .eq(comparator_5_eq));  // open: gt, lt
  Comparator comparator_6 (.a(register_1_q_2[39:32]), .b(CBD3[39:32]), .eq(comparator_6_eq));  // open: gt, lt
  not not_4 (not_4_out, comparator_7_eq);
  Comparator comparator_7 (.a(register_1_q_2[39:32]), .b({8{1'b0}}), .eq(comparator_7_eq));  // open: gt, lt
  Pull_Resistor pull_resistor_1 (.node(pull_resistor_1_node));
  Priority_Encoder #(.select(2)) priority_encoder_1 (
    .in0(1'b0), .in1(comparator_4_eq), .in2(comparator_5_eq), .in3(comparator_6_eq),
    .out(pull_resistor_1_node), .gs(priority_encoder_1_gs));  // open: en_out, en_in
  Multiplexer #(.select(2), .width(32)) multiplexer_2 (
    .in0(register_1_q[31:0]), .in1(CBD1[31:0]), .in2(CBD2[31:0]), .in3(CBD3[31:0]), .out(multiplexer_2_out),
    .sel(pull_resistor_1_node));
  and and_3 (and_3_out, register_1_q[43], not_4_out);
  or or_2 (register_1_q_2[43], and_3_out, and_4_out);
  and and_4 (and_4_out, priority_encoder_1_gs, not_4_out);
  Pull_Resistor pull_resistor_2 (.node(pull_resistor_2_node));
  Multiplexer #(.width(64)) multiplexer_3 (
    .in0({register_1_q_2, multiplexer_2_out}), .in1(pull_resistor_2_node), .out(ENTRY_OUT), .sel(RST));

  // Notes on the sheet:
  //   CLK: pull=down
  //   WRITE: pull=down
endmodule

module ForwardingUnit (
  input  CLK,
  input  [7:0] ROB_REG,
  input  [31:0] ROB_VALUE,
  input  [3:0] INST_DEST,
  input  [3:0] REGA_IN,
  input  [3:0] REGB_IN,
  input  [31:0] ARF_A_IN,
  input  [31:0] ARF_B_IN,
  input  WRITE_ROB,
  input  RST,
  input  [39:0] CBD1IN,
  input  [39:0] CBD2IN,
  input  [39:0] CBD3IN,
  output [39:0] CBD1,
  output [39:0] CBD2
);

  wire and_1_out, and_2_out, and_3_out, and_4_out, and_5_out, and_6_out, and_7_out, bitselector_1_out,
       bitselector_2_out, comparator_1_eq, comparator_2_eq, comparator_3_eq, comparator_4_eq,
       comparator_5_eq, comparator_6_eq, comparator_7_eq, decoder_1_out1, decoder_1_out2, decoder_1_out3,
       decoder_1_out4, decoder_1_out5, decoder_1_out6, decoder_1_out7, decoder_1_out8, decoder_1_out9,
       decoder_1_out10, decoder_1_out11, decoder_1_out12, decoder_1_out13, decoder_1_out14, decoder_1_out15,
       decoder_2_out1, decoder_2_out2, decoder_2_out3, decoder_2_out4, decoder_2_out5, decoder_2_out6,
       decoder_2_out7, decoder_2_out8, decoder_2_out9, decoder_2_out10, decoder_2_out11, decoder_2_out12,
       decoder_2_out13, decoder_2_out14, decoder_2_out15, not_1_out, not_2_out, not_3_out, not_4_out,
       or_1_out, or_2_out, or_3_out, or_4_out, or_5_out, or_6_out, or_7_out, or_8_out, or_9_out, or_10_out,
       or_11_out, or_12_out, or_13_out, or_14_out, or_15_out, priority_encoder_1_p1;
  wire [1:0] priority_encoder_1_p3, priority_encoder_2_p3;
  wire [3:0] bit_extender_1_out, cbdsplitter_5_halfregid, cbdsplitter_6_halfregid;
  wire [7:0] cbdsplitter_1_fullregid;
  wire [14:0] s_r_ff_2_q;
  wire [39:0] cbdsplitter_4_cbdout, cbdsplitter_5_cbdout, cbdsplitter_6_cbdout;

  Bit_Extender #(.out_width(4)) bit_extender_1 (.in(ROB_REG), .out(bit_extender_1_out));
  or or_1 (or_1_out, RST, decoder_1_out2);
  or or_2 (or_2_out, RST, decoder_1_out1);
  S_R_Flip_Flop s_r_ff_1 (.Q(s_r_ff_2_q[1]), .reset(or_2_out), .preset(decoder_2_out1));  // open: S, R, clk, Qn
  S_R_Flip_Flop s_r_ff_2 (.Q(s_r_ff_2_q[0]), .reset(or_1_out), .preset(decoder_2_out2));  // open: S, R, clk, Qn
  Decoder #(.select(4)) decoder_1 (
    .out1(decoder_1_out1), .out2(decoder_1_out2), .out3(decoder_1_out3), .out4(decoder_1_out4),
    .out5(decoder_1_out5), .out6(decoder_1_out6), .out7(decoder_1_out7), .out8(decoder_1_out8),
    .out9(decoder_1_out9), .out10(decoder_1_out10), .out11(decoder_1_out11), .out12(decoder_1_out12),
    .out13(decoder_1_out13), .out14(decoder_1_out14), .out15(decoder_1_out15), .sel(bit_extender_1_out));  // open: out0, en
  or or_3 (or_3_out, RST, decoder_1_out3);
  or or_4 (or_4_out, RST, decoder_1_out4);
  CBDSplitter cbdsplitter_1 (
    .CBDIN(CBD1IN), .FullRegId(cbdsplitter_1_fullregid));  // open: ValueIn, RegIn, Value, HalfRegId, CBDOUT
  CBDSplitter cbdsplitter_2 (.CBDIN(CBD2IN));  // open: ValueIn, RegIn, Value, FullRegId, HalfRegId, CBDOUT
  CBDSplitter cbdsplitter_3 (.CBDIN(CBD3IN));  // open: ValueIn, RegIn, Value, FullRegId, HalfRegId, CBDOUT
  or or_5 (or_5_out, RST, decoder_1_out5);
  S_R_Flip_Flop s_r_ff_3 (.Q(s_r_ff_2_q[2]), .reset(or_3_out), .preset(decoder_2_out3));  // open: S, R, clk, Qn
  S_R_Flip_Flop s_r_ff_4 (.Q(s_r_ff_2_q[3]), .reset(or_4_out), .preset(decoder_2_out4));  // open: S, R, clk, Qn
  CBDSplitter cbdsplitter_4 (
    .ValueIn(ROB_VALUE), .RegIn(bit_extender_1_out), .CBDOUT(cbdsplitter_4_cbdout));  // open: CBDIN, Value, FullRegId, HalfRegId
  CBDSplitter cbdsplitter_5 (
    .ValueIn(ARF_A_IN), .RegIn(REGA_IN), .HalfRegId(cbdsplitter_5_halfregid), .CBDOUT(cbdsplitter_5_cbdout));  // open: CBDIN, Value, FullRegId
  CBDSplitter cbdsplitter_6 (
    .ValueIn(ARF_B_IN), .RegIn(REGB_IN), .HalfRegId(cbdsplitter_6_halfregid), .CBDOUT(cbdsplitter_6_cbdout));  // open: CBDIN, Value, FullRegId
  or or_6 (or_6_out, RST, decoder_1_out6);
  Decoder #(.select(4)) decoder_2 (
    .out1(decoder_2_out1), .out2(decoder_2_out2), .out3(decoder_2_out3), .out4(decoder_2_out4),
    .out5(decoder_2_out5), .out6(decoder_2_out6), .out7(decoder_2_out7), .out8(decoder_2_out8),
    .out9(decoder_2_out9), .out10(decoder_2_out10), .out11(decoder_2_out11), .out12(decoder_2_out12),
    .out13(decoder_2_out13), .out14(decoder_2_out14), .out15(decoder_2_out15), .sel(INST_DEST));  // open: out0, en
  S_R_Flip_Flop s_r_ff_5 (.Q(s_r_ff_2_q[4]), .reset(or_5_out), .preset(decoder_2_out5));  // open: S, R, clk, Qn
  S_R_Flip_Flop s_r_ff_6 (.Q(s_r_ff_2_q[5]), .reset(or_6_out), .preset(decoder_2_out6));  // open: S, R, clk, Qn
  Comparator #(.width(4)) comparator_1 (.a(bit_extender_1_out), .b(REGB_IN), .eq(comparator_1_eq));  // open: gt, lt
  or or_7 (or_7_out, RST, decoder_1_out7);
  or or_8 (or_8_out, RST, decoder_1_out8);
  BitSelector #(.width(15)) bitselector_1 (.in(s_r_ff_2_q), .out(bitselector_1_out), .sel(REGA_IN));
  Comparator #(.width(4)) comparator_2 (.a(bit_extender_1_out), .b(REGA_IN), .eq(comparator_2_eq));  // open: gt, lt
  S_R_Flip_Flop s_r_ff_7 (.Q(s_r_ff_2_q[6]), .reset(or_7_out), .preset(decoder_2_out7));  // open: S, R, clk, Qn
  S_R_Flip_Flop s_r_ff_8 (.Q(s_r_ff_2_q[7]), .reset(or_8_out), .preset(decoder_2_out8));  // open: S, R, clk, Qn
  and and_1 (and_1_out, comparator_1_eq, not_1_out);
  and and_2 (and_2_out, comparator_2_eq, not_1_out);
  not not_1 (not_1_out, comparator_3_eq);
  Comparator #(.width(4)) comparator_3 (.a(4'b0000), .b(REGA_IN), .eq(comparator_3_eq));  // open: gt, lt
  Comparator #(.width(4)) comparator_4 (
    .a(REGA_IN), .b(cbdsplitter_5_halfregid), .eq(comparator_4_eq));  // open: gt, lt
  or or_9 (or_9_out, RST, decoder_1_out9);
  or or_10 (or_10_out, RST, decoder_1_out10);
  Comparator comparator_5 (.a(ROB_REG), .b(cbdsplitter_1_fullregid), .eq(comparator_5_eq));  // open: gt, lt
  and and_3 (and_3_out, not_1_out, comparator_4_eq);
  S_R_Flip_Flop s_r_ff_9 (.S(decoder_2_out9), .Q(s_r_ff_2_q[8]), .reset(or_9_out));  // open: R, clk, Qn, preset
  S_R_Flip_Flop s_r_ff_10 (.Q(s_r_ff_2_q[9]), .reset(or_10_out), .preset(decoder_2_out10));  // open: S, R, clk, Qn
  and and_4 (and_4_out, comparator_5_eq, and_2_out);
  not not_2 (not_2_out, comparator_6_eq);
  Comparator #(.width(4)) comparator_6 (.a(4'b0000), .b(REGB_IN), .eq(comparator_6_eq));  // open: gt, lt
  Comparator #(.width(4)) comparator_7 (
    .a(REGB_IN), .b(cbdsplitter_6_halfregid), .eq(comparator_7_eq));  // open: gt, lt
  or or_11 (or_11_out, RST, decoder_1_out11);
  or or_12 (or_12_out, RST, decoder_1_out12);
  and and_5 (and_5_out, not_2_out, comparator_7_eq);
  S_R_Flip_Flop s_r_ff_11 (.S(decoder_2_out11), .Q(s_r_ff_2_q[10]), .reset(or_11_out));  // open: R, clk, Qn, preset
  S_R_Flip_Flop s_r_ff_12 (.Q(s_r_ff_2_q[11]), .reset(or_12_out), .preset(decoder_2_out12));  // open: S, R, clk, Qn
  BitSelector #(.width(15)) bitselector_2 (.in(s_r_ff_2_q), .out(bitselector_2_out), .sel(REGB_IN));
  not not_3 (not_3_out, bitselector_1_out);
  and and_6 (and_6_out, not_3_out, and_3_out);
  // Priority_Encoder #(.select(2)) priority_encoder_1: pin names not known; wires that end beside it: priority_encoder_1_p1, and_6_out, priority_encoder_1_p3, and_4_out
  or or_13 (or_13_out, RST, decoder_1_out13);
  or or_14 (or_14_out, RST, decoder_1_out14);
  // Probe on priority_encoder_1_p3
  Multiplexer #(.select(2), .width(40)) multiplexer_1 (
    .in0(CBD1IN), .in1(cbdsplitter_5_cbdout), .in2(cbdsplitter_4_cbdout), .out(CBD1),
    .sel(priority_encoder_1_p3));  // open: in3
  S_R_Flip_Flop s_r_ff_13 (.S(decoder_2_out13), .Q(s_r_ff_2_q[12]), .reset(or_13_out));  // open: R, clk, Qn, preset
  S_R_Flip_Flop s_r_ff_14 (.Q(s_r_ff_2_q[13]), .reset(or_14_out), .preset(decoder_2_out14));  // open: S, R, clk, Qn
  not not_4 (not_4_out, bitselector_2_out);
  and and_7 (and_7_out, not_4_out, and_5_out);
  Pull_Resistor #(.pull(1)) pull_resistor_1 (.node(priority_encoder_1_p1));
  // Priority_Encoder #(.select(2)) priority_encoder_2: pin names not known; wires that end beside it: priority_encoder_1_p1, and_7_out, priority_encoder_2_p3, and_1_out
  Multiplexer #(.select(2), .width(40)) multiplexer_2 (
    .in0(CBD2IN), .in1(cbdsplitter_6_cbdout), .in2(cbdsplitter_4_cbdout), .out(CBD2),
    .sel(priority_encoder_2_p3));  // open: in3
  or or_15 (or_15_out, RST, decoder_1_out15);
  Pull_Resistor pull_resistor_2 (.node(CBD1));
  Pull_Resistor pull_resistor_3 (.node(CBD2));
  S_R_Flip_Flop s_r_ff_15 (.Q(s_r_ff_2_q[14]), .reset(or_15_out), .preset(decoder_2_out15));  // open: S, R, clk, Qn

  // Notes on the sheet:
  //   CBD1: pull=down
  //   CBD2: pull=down
  //   WRITE_ROB: pull=down
  //   ROB_REG: pull=down
  //   INST_DEST: pull=down
  //   CLK: pull=down
  //   ROB_VALUE: pull=down
  //   REGA_IN: pull=down
  //   REGB_IN: pull=down
  //   ARF_A_IN: pull=down
  //   ARF_B_IN: pull=down
endmodule

module CBDSplitter (
  input  [39:0] CBDIN,
  input  [31:0] ValueIn,
  input  [3:0] RegIn,
  output [31:0] Value,
  output [7:0] FullRegId,
  output [3:0] HalfRegId,
  output [39:0] CBDOUT
);

  assign CBDOUT[39:32] = {{4{1'b0}}, RegIn};  // Bit_Extender bit_extender_1
  Bit_Extender #(.out_width(4), .\type ("zero")) bit_extender_2 (.in(CBDIN[39:32]), .out(HalfRegId));

  assign CBDOUT[31:0] = ValueIn;
  assign FullRegId = CBDIN[39:32];
  assign Value = CBDIN[31:0];

  // Notes on the sheet:
  //   CBDOUT: pull=down
  //   ValueIn: pull=down
  //   RegIn: pull=down
endmodule
